# Fritzing sketch Alarma IOT (saved by Fritzing 1.0.4)

parts:
  DC1 = DC_DC_XL4016 [package=board_screw]
  Mod2 = KY-019 5V Relay Module [package="Breakout board"]
  Mod3 = KY-019 5V Relay Module [package="Breakout board"]
  SP1 = SPEAKER [package=pcb_mount_speaker]
  SP2 = SPEAKER [package=pcb_mount_speaker]
  MH-ET_LIVE_ESP32_DEVKIT1 = MH-ET LIVE ESP32 DEVKIT 38 pins
  R1 = Resistor [tolerance=±5% resistance=220 package="2512 [SMD]"]
  R2 = Resistor [tolerance=±5% resistance=220 package="2512 [SMD]"]
  R3 = Resistor [tolerance=±5% resistance=220 package="0402 [SMD]"]
  R4 = Resistor [tolerance=±5% resistance=220 package="0402 [SMD]"]
  R5 = Resistor [tolerance=±5% resistance=220 package="0402 [SMD]"]
  S1 = Pushbutton [package=THT]
  S2 = Pushbutton [package=THT]
  S3 = Pushbutton [package=THT]
  S4 = Pushbutton [package=THT]
  S5 = Pushbutton [package=THT]
  R6 = Resistor [tolerance=±5% resistance=220 package="0402 [SMD]"]  # not connected
  R7 = Resistor [tolerance=±5% resistance=220 package="0402 [SMD]"]  # not connected
  R8 = Resistor [tolerance=±5% resistance=220 package="0402 [SMD]"]  # not connected
  R9 = Resistor [tolerance=±5% resistance=220 package="0402 [SMD]"]  # not connected
  R10 = Resistor [tolerance=±5% resistance=220 package="0402 [SMD]"]
  C1 = Ceramic Capacitor [capacitance=100nF voltage=35V package="100 mil [THT, multilayer]"]
  C2 = Ceramic Capacitor [capacitance=100nF voltage=35V package="100 mil [THT, multilayer]"]
  C3 = Ceramic Capacitor [capacitance=100nF voltage=35V package="100 mil [THT, multilayer]"]
  C4 = Ceramic Capacitor [capacitance=100nF voltage=35V package="100 mil [THT, multilayer]"]
  C5 = Ceramic Capacitor [capacitance=100nF voltage=35V package="100 mil [THT, multilayer]"]

nets:
  N1: DC1.IN-, DC1.OUT-
  N2: DC1.OUT+, MH-ET_LIVE_ESP32_DEVKIT1.3V3
  N3: Mod2.S, MH-ET_LIVE_ESP32_DEVKIT1.IO17
  N4: Mod2.Common, SP1.+
  N5: Mod2.NO, SP1.-
  N6: Mod3.S, MH-ET_LIVE_ESP32_DEVKIT1.IO16
  N7: Mod3.Common, SP2.+
  N8: Mod3.NO, SP2.-
  N9: MH-ET_LIVE_ESP32_DEVKIT1.IO26, R5.Pin_1
  N10: MH-ET_LIVE_ESP32_DEVKIT1.IO27, R4.Pin_1, C2.1
  N11: MH-ET_LIVE_ESP32_DEVKIT1.IO14, R3.Pin_1, C3.1
  N12: MH-ET_LIVE_ESP32_DEVKIT1.IO12, R2.Pin_1, C4.1
  N13: MH-ET_LIVE_ESP32_DEVKIT1.IO13, R1.Pin_1, R10.Pin_1
  N14: S1.leg0, C1.0
  N15: S2.leg0, C2.0
  N16: S3.leg0, C3.0
  N17: S4.leg0, C4.0
  N18: S5.leg0, C5.0

notes:
  3.3 V
  Exterior alarm
  Interior alarm
  12 V
  Front door sensor
  Back door sensor
  Movement sensor 1
  Movement sensor 2
  Movement sensor 3

custom parts:
  KY-019 5V Relay Module: KY-019 5V Relay module, used to control AC circuits. (Special thanks to vanepp for fixing the PCB holes and other errors)
  MH-ET LIVE ESP32 DEVKIT 38 pins: http://mh.nodebb.com/topic/2/mh-et-live-esp32-devkit
